// Logisim project alu-control.circ as structural Verilog: 1 circuit, main circuit main
// ALUControl
module main (
  input  [1:0] Opcode,
  input  [5:0] Funct,
  input  [1:0] sh,
  output [3:0] ALUControl
);

  wire comparator_1_eq, comparator_2_eq;
  wire [3:0] multiplexer_1_out, multiplexer_2_out, multiplexer_3_out;

  Comparator #(.width(2)) comparator_1 (.a(2'b00), .b(Opcode), .eq(comparator_1_eq));  // open: gt, lt
  Multiplexer #(.select(2), .width(4), .enable("false")) multiplexer_1 (
    .in0(4'b0100), .in1(4'b0101), .in2(4'b0110), .out(multiplexer_1_out), .sel(sh));  // open: in3
  Multiplexer #(.select(4), .width(4)) multiplexer_2 (
    .in0(4'b0000), .in1(4'b0010), .in2(4'b1000), .in4(4'b0111), .in10(4'b1000), .in12(4'b0001),
    .in13(4'b1101), .in15(4'b0011), .out(multiplexer_2_out), .sel(Funct[4:1]), .en(comparator_1_eq));  // open: in3, in5, in6, in7, in8, in9, in11, in14
  Multiplexer #(.width(4), .enable("false")) multiplexer_3 (
    .in0(multiplexer_2_out), .in1(multiplexer_1_out), .out(multiplexer_3_out), .sel(comparator_2_eq));
  Comparator #(.width(4)) comparator_2 (.a(multiplexer_2_out), .b(4'b1101), .eq(comparator_2_eq));  // open: gt, lt
  Multiplexer #(.select(2), .width(4), .enable("false")) multiplexer_4 (
    .in0(multiplexer_3_out), .in1(4'b0111), .in2(4'b0111), .out(ALUControl), .sel(Opcode));  // open: in3

  // Other names for the same wires on the sheet: Ctrl[3:0] = ALUControl; FN[5:0] = Funct; OP[1:0] = Opcode

  // Notes on the sheet:
  //   shifts
  //   data-processing
  //   DO NOT MOVE, CHANGE, ADD, OR REMOVE INPUTS AND OUTPUTS!!!
  //   Hongwei Cai
  //   ARM Processor
  //   Spring 2022
  //   Computer Organization
endmodule
