// Logisim project control.circ as structural Verilog: 3 circuits, main circuit main
// Control Unit
module main (
  input  [3:0] Cond,
  input  CLK,
  input  [1:0] Op,
  input  PCSrc,
  input  [5:0] Funct,
  input  RegWrite,
  input  MemWrite,
  input  [3:0] Rd,
  input  MemtoReg,
  input  [3:0] ALUFlags,
  input  ALUSrc,
  input  [1:0] ImmSrc,
  input  [3:0] ALUControl,
  input  [1:0] RegSrc
);

  wire ALUOp, ALUSrc_t, and_2_out, and_3_out, MemW, not_1_out, not_2_out, not_3_out, not_4_out, not_5_out,
       not_6_out, PCS, RegW;
  wire [1:0] and_5_out, FlagW, undriven;

  not not_1 (not_1_out, Funct[0]);
  or or_1 (ALUSrc_t, Funct[5], Op[0], Op[1]);
  not not_2 (not_2_out, Op[1]);
  not not_3 (not_3_out, Op[0]);
  not not_4 (not_4_out, Op[1]);
  not not_5 (not_5_out, Op[1]);
  not not_6 (not_6_out, Op[0]);
  and and_1 (MemW, Op[0], not_1_out);
  and and_2 (and_2_out, not_2_out, not_3_out);
  or or_2 (RegW, and_2_out, and_3_out);
  and and_3 (and_3_out, not_4_out, Funct[0]);
  and and_4 (ALUOp, not_5_out, not_6_out);
  assign and_5_out = FlagW & undriven;  // AND_Gate and_5, 2 bits wide
  and and_6 (PCSrc, PCS, undriven[0]);
  and and_7 (RegWrite, RegW, undriven[0]);
  and and_8 (MemWrite, MemW, undriven[0]);
  // alu_control_main main_1: pin names not known

  // Other names for the same wires on the sheet: Branch = Op[1]; ImmSrc_t[1:0] = Op; RegSrc_t[1:0] = {Op[0], Op[1]};
  //   MemtoReg_t = Op[0]

  // Notes on the sheet:
  //   Main Decoder
endmodule

module subcircuit1 (
);

  wire ALUOp, ALUSrc, and_2_out, and_3_out, Branch, Funct0, Funct5, MemW, not_1_out, not_2_out, not_3_out,
       not_4_out, not_5_out, not_6_out, RegW;
  wire [0:0] ImmSrc;

  not not_1 (not_1_out, Funct0);
  or or_1 (ALUSrc, Funct5, ImmSrc[0], Branch);
  not not_2 (not_2_out, Branch);
  not not_3 (not_3_out, ImmSrc[0]);
  not not_4 (not_4_out, Branch);
  not not_5 (not_5_out, Branch);
  not not_6 (not_6_out, ImmSrc[0]);
  and and_1 (MemW, ImmSrc[0], not_1_out);
  and and_2 (and_2_out, not_2_out, not_3_out);
  or or_2 (RegW, and_2_out, and_3_out);
  and and_3 (and_3_out, not_4_out, Funct0);
  and and_4 (ALUOp, not_5_out, not_6_out);

  // Other names for the same wires on the sheet: ImmSrc[1] = Branch; Op[1:0] = {Branch, ImmSrc[0]};
  //   RegSrc[1:0] = {ImmSrc[0], Branch}; MemtoReg = ImmSrc[0]
endmodule

module subcircuit (
  input  Op1,
  input  Op0,
  input  Funct5,
  input  Funct0,
  output Branch,
  output MemtoReg,
  output MemW,
  output ALUSrc,
  output ImmSrc1,
  output ImmSrc0,
  output RegW,
  output RegSrc1,
  output RegSrc0,
  output ALUOp
);

  wire decoder_1_out0, decoder_1_out1, decoder_1_out2, decoder_2_out0, decoder_2_out1, decoder_3_out0,
       decoder_3_out1, DP_Imm_out, DP_Reg_out, Funct0_t, Funct5_t, LDR_out, not_1_out, not_2_out, not_3_out,
       not_4_out, not_5_out, STR_out;
  wire [1:0] Op;

  Decoder #(.select(2), .enable("false")) decoder_1 (
    .out0(decoder_1_out0), .out1(decoder_1_out1), .out2(decoder_1_out2), .sel(Op));  // open: out3
  Decoder #(.enable("false")) decoder_2 (.out0(decoder_2_out0), .out1(decoder_2_out1), .sel(Funct0_t));
  Decoder #(.enable("false")) decoder_3 (.out0(decoder_3_out0), .out1(decoder_3_out1), .sel(Funct5_t));
  and DP_Reg (DP_Reg_out, decoder_1_out0, decoder_3_out0);
  and DP_Imm (DP_Imm_out, decoder_1_out0, decoder_3_out1);
  and STR (STR_out, decoder_1_out1, decoder_2_out0);
  and LDR (LDR_out, decoder_1_out1, decoder_2_out1);
  not not_1 (not_1_out, decoder_1_out2);
  not not_2 (not_2_out, DP_Reg_out);
  not not_3 (not_3_out, DP_Imm_out);
  not not_4 (not_4_out, STR_out);
  not not_5 (not_5_out, LDR_out);
endmodule
