// Logisim project cpu.circ as structural Verilog: 1 circuit, main circuit main
module main (
  input  [31:0] INSTRUCTION,
  input  CLOCK,
  output [31:0] FETCH_ADDRESS,
  output [31:0] R0_Value,
  output [31:0] R1_Value,
  output [31:0] R2_Value,
  output [31:0] LR_Value,
  output [31:0] SP_Value
);

  wire ALUSrc, comparator_1_eq, MemtoReg, MemWrite, MOV_out, PCSrc, RegWrite;
  wire [1:0] ImmSrc, RegSrc;
  wire [3:0] ALUControl, ALUFlags, RA1, RA2;
  wire [31:0] adder_1_out, adder_3_out, Data_Memory_read_data, ExtImm8, ExtImm12, ExtImm24,
       main_1_read_data_1, main_3_result, multiplexer_1_out, multiplexer_4_out, multiplexer_6_out,
       multiplier_1_out, PC, RD2, SrcB, WD;

  Multiplexer #(.width(32), .enable("false")) multiplexer_1 (
    .in0(adder_1_out), .in1(WD), .out(multiplexer_1_out), .sel(PCSrc));
  Register #(.width(32)) u_PC (.D(multiplexer_1_out), .Q(FETCH_ADDRESS), .clk(CLOCK));  // open: en, clr
  Multiplexer #(.width(4), .enable("false")) multiplexer_2 (
    .in0(INSTRUCTION[19:16]), .in1(4'b1111), .out(RA1), .sel(RegSrc[1]));
  Multiplexer #(.width(4), .enable("false")) multiplexer_3 (
    .in0(INSTRUCTION[3:0]), .in1(INSTRUCTION[15:12]), .out(RA2), .sel(RegSrc[0]));
  assign ExtImm8 = {{24{1'b0}}, INSTRUCTION[7:0]};  // Bit_Extender bit_extender_1
  assign ExtImm12 = {{20{1'b0}}, INSTRUCTION[11:0]};  // Bit_Extender bit_extender_2
  assign ExtImm24 = {{8{INSTRUCTION[23]}}, INSTRUCTION[23:0]};  // Bit_Extender bit_extender_3
  Adder #(.width(32)) adder_1 (.a(FETCH_ADDRESS), .b(32'h4), .out(adder_1_out));  // open: cin, cout
  Adder #(.width(32)) adder_2 (.a(adder_1_out), .b(32'h4), .out(PC));  // open: cin, cout
  Multiplier #(.width(32)) multiplier_1 (.a(ExtImm24), .b(32'h4), .out(multiplier_1_out));  // open: cin, cout
  Adder #(.width(32)) adder_3 (.a(multiplier_1_out), .b(32'h8), .out(adder_3_out));  // open: cin, cout
  regfile_main main_1 (
    .Read_Register_1(RA1), .Read_Register_2(RA2), .Write_Register(INSTRUCTION[15:12]), .Write_Data(WD),
    .Write_Enable(RegWrite), .Clock(CLOCK), .Read_Data_1(main_1_read_data_1), .Read_Data_2(RD2),
    .R0_Value(R0_Value), .R1_Value(R1_Value), .R3_Value(R2_Value), .LR__R14__Value(LR_Value),
    .SP__R13__Value(SP_Value), .R15(PC));
  Multiplexer #(.select(2), .width(32), .enable("false")) multiplexer_4 (
    .in0(ExtImm8), .in1(ExtImm12), .in2(adder_3_out), .out(multiplexer_4_out), .sel(ImmSrc));  // open: in3
  control_main main_2 (
    .Cond(INSTRUCTION[31:28]), .Op(INSTRUCTION[27:26]), .Rd(INSTRUCTION[15:12]), .ALUFlags(ALUFlags),
    .CLK(CLOCK), .sh(INSTRUCTION[6:5]), .Funct(INSTRUCTION[25:20]), .PCSrc(PCSrc), .RegWrite(RegWrite),
    .MemWrite(MemWrite), .MemtoReg(MemtoReg), .ALUSrc(ALUSrc), .ImmSrc(ImmSrc), .RegSrc(RegSrc),
    .ALUControl(ALUControl));
  Multiplexer #(.width(32), .enable("false")) multiplexer_5 (
    .in0(RD2), .in1(multiplexer_4_out), .out(SrcB), .sel(ALUSrc));
  Comparator #(.width(4), .mode("unsigned")) comparator_1 (
    .a(INSTRUCTION[24:21]), .b(4'b1101), .eq(comparator_1_eq));  // open: gt, lt
  alu_main main_3 (
    .ALUControl(ALUControl), .A(main_1_read_data_1), .ALUFlags(ALUFlags), .Result(main_3_result), .B(SrcB));
  and MOV (MOV_out, comparator_1_eq, INSTRUCTION[25]);
  Multiplexer #(.width(32), .enable("false")) multiplexer_6 (
    .in0(main_3_result), .in1(SrcB), .out(multiplexer_6_out), .sel(MOV_out));
  mem_main Data_Memory (
    .Address(multiplexer_6_out), .Write_Data(RD2), .Write_En(MemWrite), .Clock(CLOCK),
    .Read_Data(Data_Memory_read_data));
  Multiplexer #(.width(32), .enable("false")) multiplexer_7 (
    .in0(multiplexer_6_out), .in1(Data_Memory_read_data), .out(WD), .sel(MemtoReg));

  // Other names for the same wires on the sheet: clk = CLOCK; fetch_addr[31:0] = FETCH_ADDRESS;
  //   sh[1:0] = INSTRUCTION[6:5]; shamt5[4:0] = INSTRUCTION[11:7]; Rd[3:0] = INSTRUCTION[15:12];
  //   Funct[5:0] = INSTRUCTION[25:20]; cmd[3:0] = INSTRUCTION[24:21]; I = INSTRUCTION[25];
  //   Op[1:0] = INSTRUCTION[27:26]; Cond[3:0] = INSTRUCTION[31:28]; R0[31:0] = R0_Value; R1[31:0] = R1_Value;
  //   R2[31:0] = R2_Value; R13[31:0] = SP_Value; R14[31:0] = LR_Value

  // Notes on the sheet:
  //   Instruction Memory
  //   Output
  //   DataProcess
  //   MemoryInstr
  //   Branch
  //   PC+4
  //   Inputs
  //   PC+8
  //   These are DEBUG/TEST outputs from your circuit.
  //   Hongwei Cai
  //   ARM Processor
  //   Computer Organization
  //   Spring 2022
  //   ReadData
endmodule
