// Logisim project cpu.circ as structural Verilog: 1 circuit, main circuit main
module main (
  input  [31:0] INSTRUCTION,
  input  CLOCK,
  output [31:0] FETCH_ADDRESS,
  output [31:0] R0_Value,
  output [31:0] R1_Value,
  output [31:0] R2_Value,
  output [31:0] LR_Value,
  output [31:0] SP_Value
);

  wire comparator_1_eq;
  wire [31:0] adder_1_out, main_1_read_data_1, main_1_read_data_2;

  Register #(.width(32)) PC (.clk(CLOCK));  // open: D, en, Q, clr
  Comparator #(.width(4)) comparator_1 (.a(INSTRUCTION[24:21]), .b(4'b0110), .eq(comparator_1_eq));  // open: gt, lt
  regfile_main main_1 (
    .Read_Register_1(INSTRUCTION[3:0]), .Read_Register_2(INSTRUCTION[15:12]),
    .Write_Register(INSTRUCTION[19:16]), .Write_Data(adder_1_out), .Write_Enable(comparator_1_eq),
    .Clock(CLOCK), .Read_Data_1(main_1_read_data_1), .Read_Data_2(main_1_read_data_2), .R0_Value(R0_Value),
    .R1_Value(R1_Value), .R2_Value(R2_Value), .LR__R14__Value(LR_Value), .SP__R13__Value(SP_Value));  // open: R15
  Adder #(.width(32)) adder_1 (.a(main_1_read_data_1), .b(main_1_read_data_2), .out(adder_1_out));  // open: cin, cout

  // Other names for the same wires on the sheet: clk = CLOCK; fetch_addr[31:0] = FETCH_ADDRESS; R0[31:0] = R0_Value;
  //   R1[31:0] = R1_Value; R2[31:0] = R2_Value; R13[31:0] = SP_Value; R14[31:0] = LR_Value

  // Notes on the sheet:
  //   Output
  //   Inputs
  //   These are DEBUG/TEST outputs from your circuit.
  //   Hongwei Cai
  //   Spring 2022
  //   Computer Organization
endmodule
